// Logisim project Control Circuit.circ as structural Verilog: 1 circuit, main circuit main
module main (
  input  _31,
  input  _30,
  input  _29,
  input  _28,
  input  _27,
  input  _26
);

  wire addi_out, and_1_out, and_2_out, branch_out, jal_out, jump_out, lb_out, lbu_out, lw_out, or_1_out,
       or_2_out, or_3_out, or_4_out, Rtype_out, sb_out, slti_out, sw_out;

  and Rtype (Rtype_out, ~_31, ~_30, ~_29, ~_28, ~_27, ~_26);  // AND_Gate
  and jump (jump_out, ~_31, ~_30, ~_29, ~_28, _27, ~_26);  // AND_Gate
  and jal (jal_out, ~_31, ~_30, ~_29, ~_28, _27, _26);  // AND_Gate
  and branch (branch_out, ~_31, ~_30, ~_29, _28, ~_27, ~_26);  // AND_Gate
  and addi (addi_out, ~_31, ~_30, _29, ~_28, ~_27, ~_26);  // AND_Gate
  and slti (slti_out, ~_31, ~_30, _29, ~_28, _27, ~_26);  // AND_Gate
  and lb (lb_out, _31, ~_30, ~_29, ~_28, ~_27, ~_26);  // AND_Gate
  and lbu (lbu_out, _31, ~_30, ~_29, _28, ~_27, ~_26);  // AND_Gate
  and lw (lw_out, _31, ~_30, ~_29, ~_28, _27, _26);  // AND_Gate
  and sb (sb_out, _31, ~_30, _29, ~_28, ~_27, ~_26);  // AND_Gate
  and sw (sw_out, _31, ~_30, _29, ~_28, _27, _26);  // AND_Gate
  or or_1 (or_1_out, jump_out, jal_out);
  or or_2 (or_2_out, lb_out, lbu_out, lw_out);
  or or_3 (or_3_out, Rtype_out, slti_out);
  or or_4 (or_4_out, sb_out, sw_out);
  and and_1 (and_1_out, ~Rtype_out, ~branch_out);  // AND_Gate
  and and_2 (and_2_out, ~sw_out, ~jump_out, ~branch_out, ~sb_out);  // AND_Gate

  // Notes on the sheet:
  //   RegDst1
  //   RegDst2
  //   Jump
  //   Branch
  //   MemToReg1
  //   MemToReg2
  //   MemRead
  //   AluOp1
  //   AluOp2
  //   MemWrite
  //   AluSrc
  //   RegWrite
endmodule
